// Logisim project johndoe31415_lib.circ as structural Verilog: 4 circuits, main circuit IC7447
module IC7447 (
  input  Ain,
  input  Bin,
  input  Cin,
  input  Din,
  input  BI,
  input  LT,
  input  RBI,
  output a,
  output b,
  output c,
  output d,
  output e,
  output RBO,
  output f,
  output g
);

  wire and_1_out, and_2_out, and_3_out, and_4_out, and_5_out, and_6_out, and_7_out, and_8_out, and_9_out,
       and_10_out, and_11_out, and_12_out, and_13_out, and_14_out, and_15_out, and_16_out, and_17_out,
       and_18_out, buffer_1_out, buffer_2_out, buffer_3_out, nand_1_out, nand_2_out, nand_3_out, nand_5_out,
       nand_6_out, nand_7_out, nand_8_out, nor_1_out, nor_2_out, nor_3_out, nor_4_out, nor_5_out, nor_6_out,
       nor_7_out, not_1_out, not_2_out;

  nand nand_1 (nand_1_out, Ain, buffer_1_out);
  nand nand_2 (nand_2_out, Bin, buffer_1_out);
  nand nand_3 (nand_3_out, Cin, buffer_1_out);
  not not_1 (not_1_out, Din);
  buf buffer_1 (buffer_1_out, LT);
  not not_2 (not_2_out, RBI);
  buf buffer_2 (buffer_2_out, and_1_out);
  and and_1 (and_1_out, BI, RBO);
  nand nand_4 (RBO, buffer_1_out, not_2_out, not_1_out, nand_3_out, nand_2_out, nand_1_out);
  nand nand_5 (nand_5_out, nand_1_out, buffer_2_out);
  nand nand_6 (nand_6_out, nand_2_out, buffer_2_out);
  nand nand_7 (nand_7_out, nand_3_out, buffer_2_out);
  nand nand_8 (nand_8_out, not_1_out, buffer_2_out);
  and and_2 (and_2_out, nand_6_out, nand_8_out);
  and and_3 (and_3_out, nand_1_out, nand_7_out);
  and and_4 (and_4_out, nand_5_out, nand_2_out, nand_3_out, not_1_out);
  and and_5 (and_5_out, nand_6_out, nand_8_out);
  and and_6 (and_6_out, nand_5_out, nand_2_out, nand_7_out);
  and and_7 (and_7_out, nand_1_out, nand_6_out, nand_7_out);
  and and_8 (and_8_out, nand_7_out, nand_8_out);
  and and_9 (and_9_out, nand_1_out, nand_6_out, nand_3_out);
  and and_10 (and_10_out, nand_5_out, nand_2_out, nand_3_out);
  and and_11 (and_11_out, nand_1_out, nand_2_out, nand_7_out);
  and and_12 (and_12_out, nand_5_out, nand_6_out, nand_7_out);
  buf buffer_3 (buffer_3_out, nand_5_out);
  and and_13 (and_13_out, nand_2_out, nand_7_out);
  and and_14 (and_14_out, nand_5_out, nand_6_out);
  and and_15 (and_15_out, nand_6_out, nand_3_out);
  and and_16 (and_16_out, nand_5_out, nand_3_out, not_1_out);
  and and_17 (and_17_out, nand_5_out, nand_6_out, nand_7_out);
  and and_18 (and_18_out, nand_2_out, nand_3_out, not_1_out, buffer_1_out);
  nor nor_1 (nor_1_out, and_2_out, and_3_out, and_4_out);
  not not_3 (a, nor_1_out);
  nor nor_2 (nor_2_out, and_5_out, and_6_out, and_7_out);
  not not_4 (b, nor_2_out);
  nor nor_3 (nor_3_out, and_8_out, and_9_out);
  not not_5 (c, nor_3_out);
  nor nor_4 (nor_4_out, and_10_out, and_11_out, and_12_out);
  not not_6 (d, nor_4_out);
  nor nor_5 (nor_5_out, buffer_3_out, and_13_out);
  not not_7 (e, nor_5_out);
  nor nor_6 (nor_6_out, and_14_out, and_15_out, and_16_out);
  not not_8 (f, nor_6_out);
  nor nor_7 (nor_7_out, and_17_out, and_18_out);
  not not_9 (g, nor_7_out);

  // Notes on the sheet:
  //   BI: pull=up
  //   LT: pull=up
  //   RBI: pull=up
  //   Transcribed from Texas Instruments SDLS111 - March 1974 - Revised March 1988
  //   SN5446A, 47A, 48, SN54LS47, LS48, LS49, SN7446A, 47A, SN74LS47, LS48, LS49 BCD-to-seven-segment decoders/drivers
endmodule

module IC74181 (
  input  S3,
  input  S2,
  input  S1,
  input  S0,
  input  B3,
  input  A3,
  input  B2,
  input  A2,
  input  B1,
  input  A1,
  input  B0,
  input  A0,
  input  M,
  input  C_n,
  output G,
  output Cnp4,
  output P,
  output F3,
  output F2,
  output AeqB,
  output F1,
  output F0
);

  wire and_1_out, and_2_out, and_3_out, and_4_out, and_5_out, and_6_out, and_7_out, and_8_out, and_9_out,
       and_10_out, and_11_out, and_12_out, and_13_out, and_14_out, and_15_out, and_16_out, and_17_out,
       and_18_out, and_19_out, and_20_out, and_21_out, and_22_out, and_23_out, and_24_out, and_25_out,
       and_26_out, and_27_out, and_28_out, and_29_out, buffer_1_out, buffer_2_out, buffer_3_out,
       buffer_4_out, buffer_5_out, buffer_6_out, buffer_7_out, buffer_8_out, buffer_9_out, buffer_10_out,
       buffer_11_out, buffer_12_out, buffer_13_out, buffer_14_out, buffer_15_out, buffer_16_out,
       buffer_17_out, buffer_18_out, buffer_19_out, nand_1_out, nand_2_out, nand_3_out, nor_1_out, nor_2_out,
       nor_3_out, nor_4_out, nor_5_out, nor_6_out, nor_7_out, nor_8_out, nor_9_out, nor_10_out, nor_11_out,
       nor_12_out, not_1_out, not_2_out, not_3_out, not_4_out, not_5_out, or_1_out, xor_1_out, xor_2_out,
       xor_3_out, xor_4_out, xor_5_out, xor_6_out, xor_7_out, xor_8_out;

  buf buffer_1 (buffer_1_out, S3);
  buf buffer_2 (buffer_2_out, S2);
  buf buffer_3 (buffer_3_out, S1);
  buf buffer_4 (buffer_4_out, S0);
  buf buffer_5 (buffer_5_out, B3);
  buf buffer_6 (buffer_6_out, A3);
  buf buffer_7 (buffer_7_out, B2);
  buf buffer_8 (buffer_8_out, A2);
  buf buffer_9 (buffer_9_out, B1);
  buf buffer_10 (buffer_10_out, A1);
  buf buffer_11 (buffer_11_out, B0);
  buf buffer_12 (buffer_12_out, A0);
  buf buffer_13 (buffer_13_out, M);
  buf buffer_14 (buffer_14_out, C_n);
  not not_1 (not_1_out, buffer_13_out);
  not not_2 (not_2_out, buffer_5_out);
  not not_3 (not_3_out, buffer_7_out);
  not not_4 (not_4_out, buffer_9_out);
  not not_5 (not_5_out, buffer_11_out);
  buf buffer_15 (buffer_15_out, buffer_6_out);
  buf buffer_16 (buffer_16_out, buffer_8_out);
  buf buffer_17 (buffer_17_out, buffer_10_out);
  buf buffer_18 (buffer_18_out, buffer_12_out);
  and and_1 (and_1_out, buffer_5_out, buffer_1_out, buffer_6_out);
  and and_2 (and_2_out, buffer_6_out, buffer_2_out, not_2_out);
  and and_3 (and_3_out, not_2_out, buffer_3_out);
  and and_4 (and_4_out, buffer_4_out, buffer_5_out);
  and and_5 (and_5_out, buffer_7_out, buffer_1_out, buffer_8_out);
  and and_6 (and_6_out, buffer_8_out, buffer_2_out, not_3_out);
  and and_7 (and_7_out, not_3_out, buffer_3_out);
  and and_8 (and_8_out, buffer_4_out, buffer_7_out);
  and and_9 (and_9_out, buffer_9_out, buffer_1_out, buffer_10_out);
  and and_10 (and_10_out, buffer_10_out, buffer_2_out, not_4_out);
  and and_11 (and_11_out, not_4_out, buffer_3_out);
  and and_12 (and_12_out, buffer_4_out, buffer_9_out);
  and and_13 (and_13_out, buffer_11_out, buffer_1_out, buffer_12_out);
  and and_14 (and_14_out, buffer_12_out, buffer_2_out, not_5_out);
  and and_15 (and_15_out, not_5_out, buffer_3_out);
  and and_16 (and_16_out, buffer_4_out, buffer_11_out);
  nor nor_1 (nor_1_out, and_1_out, and_2_out);
  nor nor_2 (nor_2_out, and_3_out, and_4_out, buffer_15_out);
  nor nor_3 (nor_3_out, and_5_out, and_6_out);
  nor nor_4 (nor_4_out, and_7_out, and_8_out, buffer_16_out);
  nor nor_5 (nor_5_out, and_9_out, and_10_out);
  nor nor_6 (nor_6_out, and_11_out, and_12_out, buffer_17_out);
  nor nor_7 (nor_7_out, and_13_out, and_14_out);
  nor nor_8 (nor_8_out, and_15_out, and_16_out, buffer_18_out);
  xor xor_1 (xor_1_out, nor_3_out, nor_4_out);
  xor xor_2 (xor_2_out, nor_5_out, nor_6_out);
  xor xor_3 (xor_3_out, nor_7_out, nor_8_out);
  xor xor_4 (xor_4_out, nor_1_out, nor_2_out);
  buf buffer_19 (buffer_19_out, nor_2_out);
  and and_17 (and_17_out, nor_1_out, nor_4_out);
  and and_18 (and_18_out, nor_1_out, nor_3_out, nor_6_out);
  and and_19 (and_19_out, nor_1_out, nor_3_out, nor_5_out, nor_8_out);
  nand nand_1 (nand_1_out, nor_1_out, nor_3_out, nor_5_out, nor_7_out, buffer_14_out);
  nand nand_2 (nand_2_out, nor_1_out, nor_3_out, nor_5_out, nor_7_out);
  nand nand_3 (nand_3_out, buffer_14_out, not_1_out);
  nor nor_9 (nor_9_out, buffer_19_out, and_17_out, and_18_out, and_19_out);
  and and_20 (and_20_out, buffer_14_out, nor_7_out, nor_5_out, nor_3_out, not_1_out);
  and and_21 (and_21_out, nor_5_out, nor_3_out, nor_8_out, not_1_out);
  and and_22 (and_22_out, nor_3_out, nor_6_out, not_1_out);
  and and_23 (and_23_out, nor_4_out, not_1_out);
  and and_24 (and_24_out, buffer_14_out, nor_7_out, nor_5_out, not_1_out);
  and and_25 (and_25_out, nor_5_out, nor_8_out, not_1_out);
  and and_26 (and_26_out, nor_6_out, not_1_out);
  and and_27 (and_27_out, buffer_14_out, nor_7_out, not_1_out);
  and and_28 (and_28_out, nor_8_out, not_1_out);
  nor nor_10 (nor_10_out, and_20_out, and_21_out, and_22_out, and_23_out);
  nor nor_11 (nor_11_out, and_24_out, and_25_out, and_26_out);
  nor nor_12 (nor_12_out, and_27_out, and_28_out);
  or or_1 (or_1_out, ~nor_9_out, ~nand_1_out);  // OR_Gate
  xor xor_5 (xor_5_out, xor_4_out, nor_10_out);
  xor xor_6 (xor_6_out, xor_1_out, nor_11_out);
  xor xor_7 (xor_7_out, xor_2_out, nor_12_out);
  xor xor_8 (xor_8_out, xor_3_out, nand_3_out);
  and and_29 (and_29_out, xor_5_out, xor_6_out, xor_7_out, xor_8_out);
  buf buffer_20 (F0, xor_8_out);
  buf buffer_21 (G, nor_9_out);
  buf buffer_22 (Cnp4, or_1_out);
  buf buffer_23 (P, nand_2_out);
  buf buffer_24 (F3, xor_5_out);
  buf buffer_25 (F2, xor_6_out);
  buf buffer_26 (AeqB, and_29_out);
  buf buffer_27 (F1, xor_7_out);

  // Notes on the sheet:
  //   Transcribed from Philips Semiconductors 1998 Jun 10
  //   74HC/HCT181 4-bit arithmetic logic unit
endmodule

module IC74185 (
  input  A,
  input  B,
  input  C,
  input  D,
  input  E,
  input  G,
  output Y1,
  output Y2,
  output Y3,
  output Y4,
  output Y5,
  output Y6,
  output Y7,
  output Y8
);

  ROM #(.addrWidth(6)) rom_1 (.addr({G, E, D, C, B, A}), .data({Y8, Y7, Y6, Y5, Y4, Y3, Y2, Y1}));

  // Notes on the sheet:
  //   Transcribed from Texas Instruments February 1971 - Revised Decmber 1972
  //   Types SN54184, SN54185A, SN74184, SN74185A BCD-to-binary and binary-to-BCD converters
  //   contents of rom_1 (hex, n*v repeats v):
  //   c0 c1 c2 c3 c4 c8 c9 ca cb cc d0 d1 d2 d3 d4 d8 d9 da db dc e0 e1 e2 e3 e4 e8 e9 ea eb ec f0 f1
  //   32*ff
endmodule

module DHM185 (
  input  A,
  input  B,
  input  C,
  input  D,
  input  E,
  input  G,
  output Y1,
  output Y2,
  output Y3,
  output Y4,
  output Y5,
  output Y6
);

  wire [7:6] rom_1_data;

  ROM #(.addrWidth(6)) rom_1 (.addr({G, E, D, C, B, A}), .data({rom_1_data, Y6, Y5, Y4, Y3, Y2, Y1}));

  // Notes on the sheet:
  //   Simplified IC that fulfills similar functionality as the 74185, but without the LSB bypass
  //   contents of rom_1 (hex, n*v repeats v):
  //   0 1 2 3 4 5 6 7 8 9 10 11 12 13 14 15 16 17 18 19 20 21 22 23 24 25 26 27 28 29 30 31 32*ff
endmodule
