// Logisim project testbench.circ as structural Verilog: 4 circuits, main circuit IC74181_Test
module IC7447_Test (
);

  wire button_1_out, button_2_out, button_3_out, button_4_out, button_5_out, button_6_out, button_7_out,
       button_8_out, ic7447_1_rbo, ic7447_2_rbo;
  wire [3:0] counter_1_q, counter_2_q, counter_3_q, counter_4_q;
  wire [6:0] ic7447_1_a, ic7447_2_a, ic7447_3_a, ic7447_4_a;

  Button button_1 (.out(button_1_out));
  Button button_2 (.out(button_2_out));
  Button button_3 (.out(button_3_out));
  Button button_4 (.out(button_4_out));
  Button button_5 (.out(button_5_out));
  Button button_6 (.out(button_6_out));
  Button button_7 (.out(button_7_out));
  Button button_8 (.out(button_8_out));
  Counter #(.max('hf), .width(4)) counter_1 (
    .clr(button_1_out), .clk(button_2_out), .Q(counter_1_q));  // open: load, up, count, D, carry
  Counter #(.max('hf), .width(4)) counter_2 (
    .clr(button_3_out), .clk(button_4_out), .Q(counter_2_q));  // open: load, up, count, D, carry
  Counter #(.max('hf), .width(4)) counter_3 (
    .clr(button_5_out), .clk(button_6_out), .Q(counter_3_q));  // open: load, up, count, D, carry
  Counter #(.max('hf), .width(4)) counter_4 (
    .clr(button_7_out), .clk(button_8_out), .Q(counter_4_q));  // open: load, up, count, D, carry
  IC7447 ic7447_1 (
    .d(ic7447_1_a[3]), .e(ic7447_1_a[4]), .f(ic7447_1_a[5]), .g(ic7447_1_a[6]), .a(ic7447_1_a[0]),
    .b(ic7447_1_a[1]), .c(ic7447_1_a[2]), .RBO(ic7447_1_rbo), .Din(counter_1_q[3]), .RBI(1'b0),
    .Ain(counter_1_q[0]), .Bin(counter_1_q[1]), .Cin(counter_1_q[2]));  // open: BI, LT
  IC7447 ic7447_2 (
    .d(ic7447_2_a[3]), .e(ic7447_2_a[4]), .f(ic7447_2_a[5]), .g(ic7447_2_a[6]), .a(ic7447_2_a[0]),
    .b(ic7447_2_a[1]), .c(ic7447_2_a[2]), .RBO(ic7447_2_rbo), .Din(counter_2_q[3]), .RBI(ic7447_1_rbo),
    .Ain(counter_2_q[0]), .Bin(counter_2_q[1]), .Cin(counter_2_q[2]));  // open: BI, LT
  IC7447 ic7447_3 (
    .d(ic7447_3_a[3]), .e(ic7447_3_a[4]), .f(ic7447_3_a[5]), .g(ic7447_3_a[6]), .a(ic7447_3_a[0]),
    .b(ic7447_3_a[1]), .c(ic7447_3_a[2]), .Din(counter_3_q[3]), .RBI(ic7447_2_rbo), .Ain(counter_3_q[0]),
    .Bin(counter_3_q[1]), .Cin(counter_3_q[2]));  // open: RBO, BI, LT
  IC7447 ic7447_4 (
    .d(ic7447_4_a[3]), .e(ic7447_4_a[4]), .f(ic7447_4_a[5]), .g(ic7447_4_a[6]), .a(ic7447_4_a[0]),
    .b(ic7447_4_a[1]), .c(ic7447_4_a[2]), .Din(counter_4_q[3]), .Ain(counter_4_q[0]), .Bin(counter_4_q[1]),
    .Cin(counter_4_q[2]));  // open: RBO, BI, LT, RBI
  _7_Segment_Display #(.active("false"), .decimalPoint("false")) u_7_segment_display_1 (
    .g(ic7447_1_a[6]), .f(ic7447_1_a[5]), .a(ic7447_1_a[0]), .b(ic7447_1_a[1]), .e(ic7447_1_a[4]),
    .d(ic7447_1_a[3]), .c(ic7447_1_a[2]));
  _7_Segment_Display #(.active("false"), .decimalPoint("false")) u_7_segment_display_2 (
    .g(ic7447_2_a[6]), .f(ic7447_2_a[5]), .a(ic7447_2_a[0]), .b(ic7447_2_a[1]), .e(ic7447_2_a[4]),
    .d(ic7447_2_a[3]), .c(ic7447_2_a[2]));
  _7_Segment_Display #(.active("false"), .decimalPoint("false")) u_7_segment_display_3 (
    .g(ic7447_3_a[6]), .f(ic7447_3_a[5]), .a(ic7447_3_a[0]), .b(ic7447_3_a[1]), .e(ic7447_3_a[4]),
    .d(ic7447_3_a[3]), .c(ic7447_3_a[2]));
  _7_Segment_Display #(.active("false"), .decimalPoint("false")) u_7_segment_display_4 (
    .g(ic7447_4_a[6]), .f(ic7447_4_a[5]), .a(ic7447_4_a[0]), .b(ic7447_4_a[1]), .e(ic7447_4_a[4]),
    .d(ic7447_4_a[3]), .c(ic7447_4_a[2]));
endmodule

module IC74181_Test (
  input  B3,
  input  B2,
  input  B1,
  input  B0,
  input  A3,
  input  A2,
  input  A1,
  input  A0
);

  wire ic74181_1_cnp4;
  wire [0:0] not_1_out;
  wire [3:0] ic74181_1_f0;

  IC74181 ic74181_1 (
    .F2(ic74181_1_f0[2]), .F1(ic74181_1_f0[1]), .F0(ic74181_1_f0[0]), .Cnp4(ic74181_1_cnp4),
    .F3(ic74181_1_f0[3]), .B2(B2), .A2(A2), .B1(B1), .A1(A1), .B0(B0), .A0(A0), .M(1'b0), .C_n(1'b1),
    .S3(1'b1), .S2(1'b0), .S1(1'b0), .S0(1'b1), .B3(B3), .A3(A3));  // open: AeqB, G, P
  not not_1 (not_1_out[0], ic74181_1_cnp4);
  Hex_Digit_Display #(.decimalPoint("false")) hex_digit_display_1 (.value({3'b000, not_1_out[0]}));
  Hex_Digit_Display #(.decimalPoint("false")) hex_digit_display_2 (.value(ic74181_1_f0));
endmodule

module IC74185_Test (
);

  wire button_1_out, button_2_out, ic74185_2_y1, ic74185_2_y2, ic74185_2_y3, ic74185_2_y4, ic74185_2_y5,
       ic74185_2_y6, ic74185_3_y1, ic74185_3_y2, ic74185_3_y3, ic74185_3_y4, ic74185_3_y5;
  wire [2:0] ic74185_1_y4, ic74185_5_y4;
  wire [3:0] counter_2_q_2, ic74185_4_y4;
  wire [3:1] ic74185_1_y1;
  wire [5:0] counter_1_q;
  wire [8:1] counter_2_q;

  Button button_1 (.out(button_1_out));
  Button button_2 (.out(button_2_out));
  Counter #(.max('h3f), .width(6)) counter_1 (
    .clr(1'b0), .up(1'b1), .clk(button_1_out), .Q(counter_1_q));  // open: load, count, D, carry
  Counter #(.max('h1ff), .width(9)) counter_2 (
    .clr(1'b0), .up(1'b1), .clk(button_2_out), .Q({counter_2_q, counter_2_q_2[0]}));  // open: load, count, D, carry
  IC74185 ic74185_1 (
    .Y1(ic74185_1_y1[1]), .Y2(ic74185_1_y1[2]), .Y3(ic74185_1_y1[3]), .Y4(ic74185_1_y4[0]),
    .Y5(ic74185_1_y4[1]), .Y6(ic74185_1_y4[2]), .A(counter_1_q[1]), .B(counter_1_q[2]), .C(counter_1_q[3]),
    .D(counter_1_q[4]), .E(counter_1_q[5]));  // open: Y7, Y8, G
  IC74185 ic74185_2 (
    .Y1(ic74185_2_y1), .Y2(ic74185_2_y2), .Y3(ic74185_2_y3), .Y4(ic74185_2_y4), .Y5(ic74185_2_y5),
    .Y6(ic74185_2_y6), .A(counter_2_q[4]), .B(counter_2_q[5]), .C(counter_2_q[6]), .D(counter_2_q[7]),
    .E(counter_2_q[8]));  // open: Y7, Y8, G
  Hex_Digit_Display #(.decimalPoint("false")) hex_digit_display_1 (.value({ic74185_1_y1, counter_1_q[0]}));
  Hex_Digit_Display #(.decimalPoint("false")) hex_digit_display_2 (.value({1'b0, ic74185_1_y4}));
  IC74185 ic74185_3 (
    .Y1(ic74185_3_y1), .Y2(ic74185_3_y2), .Y3(ic74185_3_y3), .Y4(ic74185_3_y4), .Y5(ic74185_3_y5),
    .A(counter_2_q[2]), .B(counter_2_q[3]), .C(ic74185_2_y1), .D(ic74185_2_y2), .E(ic74185_2_y3));  // open: Y6, Y7, Y8, G
  IC74185 ic74185_4 (
    .Y1(counter_2_q_2[1]), .Y2(counter_2_q_2[2]), .Y3(counter_2_q_2[3]), .Y4(ic74185_4_y4[0]),
    .A(counter_2_q[1]), .B(ic74185_3_y1), .C(ic74185_3_y2), .D(ic74185_3_y3), .E(1'b0));  // open: Y5, Y6, Y7, Y8, G
  IC74185 ic74185_5 (
    .Y1(ic74185_4_y4[1]), .Y2(ic74185_4_y4[2]), .Y3(ic74185_4_y4[3]), .Y4(ic74185_5_y4[0]),
    .Y5(ic74185_5_y4[1]), .Y6(ic74185_5_y4[2]), .A(ic74185_3_y4), .B(ic74185_3_y5), .C(ic74185_2_y4),
    .D(ic74185_2_y5), .E(ic74185_2_y6));  // open: Y7, Y8, G
  Hex_Digit_Display #(.decimalPoint("false")) hex_digit_display_3 (.value({1'b0, ic74185_5_y4}));
  Hex_Digit_Display #(.decimalPoint("false")) hex_digit_display_4 (.value(ic74185_4_y4));
  Hex_Digit_Display #(.decimalPoint("false")) hex_digit_display_5 (.value(counter_2_q_2));
endmodule

module DHM185_Test (
);

  wire button_1_out, button_2_out, button_3_out, dhm185_2_y1, dhm185_2_y2, dhm185_2_y3, dhm185_2_y4;
  wire [1:0] dhm185_1_y5;
  wire [2:0] dhm185_3_y5;
  wire [3:0] dhm185_1_y1, dhm185_3_y1;
  wire [4:0] counter_1_q;
  wire [5:0] counter_2_q;

  Button button_1 (.out(button_1_out));
  Button button_2 (.out(button_2_out));
  Button button_3 (.out(button_3_out));
  Counter #(.max('h1f), .width(5)) counter_1 (
    .clr(1'b0), .up(1'b1), .clk(button_1_out), .Q(counter_1_q));  // open: load, count, D, carry
  Counter #(.max('h3f), .width(6)) counter_2 (
    .clr(button_2_out), .up(1'b1), .clk(button_3_out), .Q(counter_2_q));  // open: load, count, D, carry
  DHM185 dhm185_1 (
    .A(counter_1_q[0]), .B(counter_1_q[1]), .C(counter_1_q[2]), .D(counter_1_q[3]), .E(counter_1_q[4]),
    .Y1(dhm185_1_y1[0]), .Y2(dhm185_1_y1[1]), .Y3(dhm185_1_y1[2]), .Y4(dhm185_1_y1[3]), .Y5(dhm185_1_y5[0]),
    .Y6(dhm185_1_y5[1]));  // open: G
  DHM185 dhm185_2 (
    .A(counter_2_q[1]), .B(counter_2_q[2]), .C(counter_2_q[3]), .D(counter_2_q[4]), .E(counter_2_q[5]),
    .Y1(dhm185_2_y1), .Y2(dhm185_2_y2), .Y3(dhm185_2_y3), .Y4(dhm185_2_y4), .Y5(dhm185_3_y5[1]),
    .Y6(dhm185_3_y5[2]));  // open: G
  Hex_Digit_Display #(.decimalPoint("false")) hex_digit_display_1 (.value({2'b00, dhm185_1_y5}));
  Hex_Digit_Display #(.decimalPoint("false")) hex_digit_display_2 (.value(dhm185_1_y1));
  DHM185 dhm185_3 (
    .A(counter_2_q[0]), .B(dhm185_2_y1), .C(dhm185_2_y2), .D(dhm185_2_y3), .E(dhm185_2_y4),
    .Y1(dhm185_3_y1[0]), .Y2(dhm185_3_y1[1]), .Y3(dhm185_3_y1[2]), .Y4(dhm185_3_y1[3]), .Y5(dhm185_3_y5[0]));  // open: G, Y6
  Hex_Digit_Display #(.decimalPoint("false")) hex_digit_display_3 (.value({1'b0, dhm185_3_y5}));
  Hex_Digit_Display #(.decimalPoint("false")) hex_digit_display_4 (.value(dhm185_3_y1));
endmodule
